# Fritzing sketch Wiring (saved by Fritzing 0.9.3b)
breadboards: 1

parts:
  R1 = Resistor [tolerance=±5% resistance=220 package=THT]
  Part1 = Arduino Uno (Rev3)
  RHT1 = Humidity and Temperature Sensor RHT03
  U1 = ESP8266 WiFi Module [part_number=ESP8266]

nets:
  N1: R1.Pin_0, RHT1.Vcc
  N2: R1.Pin_1, Part1.D5_PWM, Part1.5V, RHT1.Data-signal
  N3: Part1.D2, U1.TXD
  N4: Part1.D3_PWM, U1.RXD
  3V3: Part1.3V3, U1.VCC, U1.CH_PD
  GND: Part1.GND, RHT1.GND_2, U1.GND

custom parts:
  ESP8266 WiFi Module: Generic WiFi Module based on the ESP8266 with onboard PCB antenna and UART communications
